# Fritzing sketch Neo 6M GPS with ESP32 (saved by Fritzing 0.9.3b)

parts:
  M1 = NEO-6M GPS Module [part_number=GY-GPS6MV2]
  esp1 = ESP32 DevKitc V4

nets:
  GND: M1.GND, esp1.GND
  N1: M1.Tx, esp1.IO16
  N2: M1.Rx, esp1.IO17
  VCC: M1.Vcc, esp1.5V

custom parts:
  NEO-6M GPS Module: GY-GPS6MV2 NEO-6M GPS Module Module based on U-blox NEO-6M GPS engine, incorporating regulator for 3.3-5V DC input, MS621FE-compatible rechargeable battery for backup and EEPROM for storing configuration settings. Links: NEO-6 series product information page NEO-6 Datasheet
  ESP32 DevKitc V4: ESP32-DevKitC board with ESP32-WROOM-32 module. ESP32-DevKitC V4 is a small-sized ESP32-based development board produced by Espressif. Most of the pins on the ESP module are broken out to the pin headers on the board. The pins D0, D1, D2, D3, CMD and CLK are used internally for communication between ESP32 and SPI flash memory. They are grouped on both sides near the USB connector. Avoid using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
